// Logisim project EIPE16.circ as structural Verilog
module EIPE16GP (
  input  SingleCycleFetch,
  input  clk,
  input  [7:0] inst_6,
  input  [7:0] inst_5,
  input  [7:0] inst_4,
  input  [7:0] inst_3,
  input  [7:0] inst_2,
  input  [7:0] inst_1,
  input  useBuiltIn,
  input  reset,
  input  Interrupt,
  input  [15:0] Peripheral1,
  input  [15:0] Peripheral2,
  input  [15:0] Peripheral3,
  input  [15:0] Peripheral4,
  input  [15:0] GA,
  output AcceptClock,
  output RequestJump,
  output RequestWrite,
  output [15:0] WriteValue,
  output [15:0] P1,
  output Pout1,
  output [15:0] P2,
  output Pout2,
  output [15:0] P3,
  output Pout3,
  output [15:0] P4,
  output Pout4,
  output [15:0] GPU,
  output RRQ,
  output ClkOut
);

  wire and_1_out, and_2_out, and_3_out, and_5_out, and_6_out, and_7_out, and_8_out, and_9_out, and_10_out,
       and_11_out, and_12_out, and_13_out, and_14_out, and_15_out, and_16_out, and_17_out, bitselector_1_out,
       BR_q, buffer_1_out, buffer_2_out, buffer_3_out, buffer_4_out, buffer_5_out, buffer_6_out,
       buffer_7_out, Bytes_carry, controlled_buffer_1_out, demultiplexer_1_out0, demultiplexer_1_out1,
       demultiplexer_1_out2, demultiplexer_1_out3, demultiplexer_1_out4, demultiplexer_1_out5,
       demultiplexer_1_out8, demultiplexer_1_out9, demultiplexer_1_out10, demultiplexer_1_out11,
       demultiplexer_1_out12, demultiplexer_1_out13, demultiplexer_1_out14, demultiplexer_1_out15,
       demultiplexer_1_out16, demultiplexer_1_out19, demultiplexer_1_out20, demultiplexer_1_out21,
       demultiplexer_1_out22, demultiplexer_1_out23, demultiplexer_1_out24, demultiplexer_1_out25,
       demultiplexer_1_out26, demultiplexer_1_out27, demultiplexer_1_out29, demultiplexer_1_out30,
       demultiplexer_1_out31, demultiplexer_2_out0, demultiplexer_2_out1, demultiplexer_2_out2,
       demultiplexer_2_out3, demultiplexer_2_out5, not_1_out, not_2_out, not_3_out, not_4_out, not_5_out,
       not_6_out, or_2_out, or_3_out, or_4_out, or_5_out, or_6_out, or_7_out, or_8_out, or_9_out, or_10_out,
       s_r_ff_1_qn, s_r_ff_2_q, s_r_ff_2_qn, t_ff_1_q, t_ff_1_qn;
  wire [4:0] bitselector_2_out, bitselector_4_out, bitselector_5_out, bitselector_6_out, bitselector_7_out,
       bitselector_8_out, bitselector_9_out;
  wire [7:0] adder_1_out, controlled_buffer_3_out, controlled_buffer_4_out, controlled_buffer_5_out,
       controlled_buffer_6_out, controlled_buffer_7_out, controlled_buffer_8_out, controlled_buffer_9_out,
       DebugInst_data, InstructionChip_data, InstructionLUT_data, MicroInstOffset_q, multiplexer_1_out,
       multiplexer_2_out, register_2_q;
  wire [15:0] ALU_1_carry, ALU_1_out_6, bit_extender_1_out, bitselector_3_out, CARRY_q, counter_1_q,
       counter_2_q, demultiplexer_3_out0, demultiplexer_3_out1, demultiplexer_3_out2, demultiplexer_3_out3,
       demultiplexer_3_out5, demultiplexer_3_out7, multiplexer_3_out, multiplexer_4_out, multiplexer_5_out,
       multiplexer_6_out, nand_1_out, R1_q, R2_q, R3_q, R4_q, register_1_q, Stack_dout;
  wire [47:0] shift_register_1_out;

  Register #(.width(16)) register_1 (
    .D(WriteValue), .en(RequestJump), .Q(register_1_q), .clk(RequestJump));  // open: clr
  and and_1 (and_1_out, not_1_out, t_ff_1_qn);
  and and_2 (and_2_out, RequestJump, and_14_out);
  not not_1 (not_1_out, and_2_out);
  buf buffer_1 (buffer_1_out, clk);
  buf buffer_2 (buffer_2_out, buffer_1_out);
  assign controlled_buffer_1_out = reset ? reset : 1'bz;  // Controlled_Buffer controlled_buffer_1
  not not_2 (not_2_out, reset);
  assign controlled_buffer_1_out = not_2_out ? Interrupt : 1'bz;  // Controlled_Buffer controlled_buffer_2
  Counter #(.max('hffff), .trigger("falling"), .width(16)) counter_1 (
    .load(and_2_out), .D(register_1_q), .count(and_1_out), .Q(counter_1_q), .clk(and_3_out), .clr(reset));  // open: carry, up
  and and_3 (and_3_out, clk, s_r_ff_1_qn);
  not not_3 (not_3_out, buffer_2_out);
  ROM #(.addrWidth(16)) DebugInst (.addr(counter_1_q), .data(DebugInst_data));
  S_R_Flip_Flop s_r_ff_1 (
    .S(demultiplexer_1_out22), .clk(not_3_out), .R(controlled_buffer_1_out), .Qn(s_r_ff_1_qn),
    .reset(controlled_buffer_1_out));  // open: Q, preset
  and and_4 (AcceptClock, t_ff_1_qn, s_r_ff_1_qn);
  S_R_Flip_Flop s_r_ff_2 (
    .clk(and_14_out), .Q(s_r_ff_2_q), .Qn(s_r_ff_2_qn), .preset(demultiplexer_1_out29), .reset(t_ff_1_qn));  // open: S, R
  and and_5 (and_5_out, demultiplexer_1_out12, bitselector_1_out);
  and and_6 (and_6_out, demultiplexer_1_out11, ~bitselector_1_out);  // AND_Gate
  buf buffer_3 (buffer_3_out, s_r_ff_2_q);
  buf buffer_4 (buffer_4_out, buffer_3_out);
  assign bit_extender_1_out = {{8{1'b0}}, inst_1};  // Bit_Extender bit_extender_1
  or or_1 (RequestJump, RequestWrite, demultiplexer_1_out21, and_5_out, and_6_out, demultiplexer_1_out20, and_7_out, and_8_out, demultiplexer_1_out13);
  and and_7 (and_7_out, demultiplexer_1_out10, BR_q);
  and and_8 (and_8_out, demultiplexer_1_out9, ~BR_q);  // AND_Gate
  not not_4 (not_4_out, SingleCycleFetch);
  Register register_2 (
    .D(multiplexer_3_out[7:0]), .en(buffer_5_out), .Q(register_2_q), .clk(buffer_5_out));  // open: clr
  buf buffer_5 (buffer_5_out, buffer_4_out);
  Multiplexer #(.width(8)) multiplexer_1 (
    .in0(register_2_q), .in1(InstructionLUT_data), .out(multiplexer_1_out), .sel(s_r_ff_2_qn));
  Multiplexer #(.width(8)) multiplexer_2 (
    .in0(inst_1), .in1(DebugInst_data), .out(multiplexer_2_out), .sel(useBuiltIn));
  and and_9 (and_9_out, not_4_out, or_2_out);
  or or_2 (or_2_out, demultiplexer_1_out29, t_ff_1_qn);
  ROM InstructionLUT (.addr(shift_register_1_out[7:0]), .data(InstructionLUT_data));
  ROM InstructionChip (.addr(adder_1_out), .data(InstructionChip_data));
  Adder adder_1 (.a(multiplexer_1_out), .b(MicroInstOffset_q), .out(adder_1_out));  // open: cin, cout
  assign nand_1_out = ~({16{1'b0}} & CARRY_q);  // NAND_Gate nand_1, 16 bits wide
  BitSelector #(.width(16)) bitselector_1 (.in(nand_1_out), .out(bitselector_1_out), .sel(4'b1111));
  Counter #(.max('h5), .trigger("falling")) Bytes (
    .count(and_9_out), .carry(Bytes_carry), .clk(and_3_out), .clr(and_10_out));  // open: load, D, Q, up
  or or_3 (or_3_out, Bytes_carry, not_6_out);
  and and_10 (and_10_out, and_13_out, ~and_3_out);  // AND_Gate
  Counter #(.ongoal("stay")) MicroInstOffset (
    .count(t_ff_1_q), .Q(MicroInstOffset_q), .clk(and_3_out), .clr(or_2_out));  // open: load, D, carry, up
  not not_5 (not_5_out, and_3_out);
  Demultiplexer #(.select(5)) demultiplexer_1 (
    .out0(demultiplexer_1_out0), .out1(demultiplexer_1_out1), .out2(demultiplexer_1_out2),
    .out3(demultiplexer_1_out3), .out4(demultiplexer_1_out4), .out5(demultiplexer_1_out5),
    .out8(demultiplexer_1_out8), .out9(demultiplexer_1_out9), .out10(demultiplexer_1_out10),
    .out11(demultiplexer_1_out11), .out12(demultiplexer_1_out12), .out13(demultiplexer_1_out13),
    .out14(demultiplexer_1_out14), .out15(demultiplexer_1_out15), .out16(demultiplexer_1_out16),
    .out17(RequestWrite), .out18(RRQ), .out19(demultiplexer_1_out19), .out20(demultiplexer_1_out20),
    .out21(demultiplexer_1_out21), .out22(demultiplexer_1_out22), .out23(demultiplexer_1_out23),
    .out24(demultiplexer_1_out24), .out25(demultiplexer_1_out25), .out26(demultiplexer_1_out26),
    .out27(demultiplexer_1_out27), .out29(demultiplexer_1_out29), .out30(demultiplexer_1_out30),
    .out31(demultiplexer_1_out31), .in(and_14_out), .sel(bitselector_2_out));  // open: out6, out7, out28
  BitSelector #(.group(5)) bitselector_2 (.in(InstructionChip_data), .out(bitselector_2_out), .sel(1'b0));
  buf buffer_6 (buffer_6_out, not_6_out);
  buf buffer_7 (buffer_7_out, buffer_6_out);
  and and_11 (and_11_out, not_5_out, buffer_7_out);
  not not_6 (not_6_out, not_4_out);
  assign controlled_buffer_3_out = and_12_out ? multiplexer_2_out : 8'bz;  // Controlled_Buffer controlled_buffer_3
  and and_12 (and_12_out, not_4_out, t_ff_1_qn);
  // Probe on shift_register_1_out
  T_Flip_Flop #(.trigger("falling")) t_ff_1 (
    .clk(and_14_out), .Q(t_ff_1_q), .Qn(t_ff_1_qn), .preset(demultiplexer_1_out31), .reset(and_13_out));  // open: T
  and and_13 (and_13_out, demultiplexer_1_out30, and_3_out);
  assign controlled_buffer_4_out = not_6_out ? inst_4 : 8'bz;  // Controlled_Buffer controlled_buffer_4
  assign controlled_buffer_5_out = not_6_out ? inst_3 : 8'bz;  // Controlled_Buffer controlled_buffer_5
  assign controlled_buffer_6_out = not_6_out ? inst_2 : 8'bz;  // Controlled_Buffer controlled_buffer_6
  assign controlled_buffer_7_out = not_6_out ? multiplexer_2_out : 8'bz;  // Controlled_Buffer controlled_buffer_7
  Shift_Register #(.length(6), .width(8)) shift_register_1 (
    .shift(and_12_out), .in(controlled_buffer_3_out), .clk(or_4_out), .out(shift_register_1_out[7:0]),
    .load(not_6_out), .clr(reset), .d0(controlled_buffer_7_out), .q0(shift_register_1_out[47:40]),
    .d1(controlled_buffer_6_out), .q1(shift_register_1_out[39:32]), .d2(controlled_buffer_5_out),
    .q2(shift_register_1_out[31:24]), .d3(controlled_buffer_4_out), .q3(shift_register_1_out[23:16]),
    .d4(controlled_buffer_9_out), .q4(shift_register_1_out[15:8]), .d5(controlled_buffer_8_out));  // open: q5
  or or_4 (or_4_out, and_11_out, and_3_out);
  assign controlled_buffer_8_out = not_6_out ? inst_6 : 8'bz;  // Controlled_Buffer controlled_buffer_8
  assign controlled_buffer_9_out = not_6_out ? inst_5 : 8'bz;  // Controlled_Buffer controlled_buffer_9
  and and_14 (and_14_out, or_3_out, and_3_out);
  BitSelector #(.group(16), .width(1)) bitselector_3 (.in(BR_q), .out(bitselector_3_out), .sel(1'b0));
  delayer The_Tower (.in_1(and_14_out), .in_2(3'b101), .out_3(ClkOut));
  Multiplexer #(.select(5), .width(16)) multiplexer_3 (
    .in0(R1_q), .in1(R2_q), .in2(R3_q), .in3(R4_q), .in4(CARRY_q), .in5(bitselector_3_out), .in6(GA),
    .in7(Peripheral1), .in8(Peripheral2), .in9(Peripheral3), .in10(Peripheral4), .in11(counter_2_q),
    .in18({shift_register_1_out[39:32], shift_register_1_out[47:40]}), .out(multiplexer_3_out),
    .sel(bitselector_4_out));  // open: in12, in13, in14, in15, in16, in17, in19, in20, in21, in22, in23, in24, in25, in26, in27, in28, in29, in30, in31
  BitSelector #(.group(5)) bitselector_4 (.in(shift_register_1_out[15:8]), .out(bitselector_4_out), .sel(1'b0));
  Multiplexer #(.select(5), .width(16)) multiplexer_4 (
    .in0(R1_q), .in1(R2_q), .in2(R3_q), .in3(R4_q), .in4(CARRY_q), .in6(GA), .in7(Peripheral1),
    .in8(Peripheral2), .in9(Peripheral3), .in10(Peripheral4), .in11(counter_2_q),
    .in18({shift_register_1_out[39:32], shift_register_1_out[47:40]}), .out(multiplexer_4_out),
    .sel(bitselector_5_out));  // open: in5, in12, in13, in14, in15, in16, in17, in19, in20, in21, in22, in23, in24, in25, in26, in27, in28, in29, in30, in31
  BitSelector #(.group(5)) bitselector_5 (.in(shift_register_1_out[23:16]), .out(bitselector_5_out), .sel(1'b0));
  or or_5 (or_5_out, demultiplexer_1_out0, demultiplexer_1_out1, demultiplexer_1_out2, demultiplexer_1_out3, demultiplexer_1_out4, demultiplexer_1_out5, demultiplexer_1_out8, demultiplexer_1_out14, demultiplexer_1_out15, demultiplexer_1_out16, RRQ, demultiplexer_1_out19, demultiplexer_1_out24, demultiplexer_1_out25, demultiplexer_1_out26, demultiplexer_1_out27);
  Register #(.width(16)) R1 (.D(demultiplexer_3_out0), .en(demultiplexer_2_out0), .Q(R1_q), .clk(ClkOut), .clr(reset));
  BitSelector #(.group(5)) bitselector_6 (.in(InstructionChip_data), .out(bitselector_6_out), .sel(1'b0));
  Demultiplexer #(.select(5)) demultiplexer_2 (
    .out0(demultiplexer_2_out0), .out1(demultiplexer_2_out1), .out2(demultiplexer_2_out2),
    .out3(demultiplexer_2_out3), .out5(demultiplexer_2_out5), .out7(Pout1), .out8(Pout2), .out9(Pout3),
    .out10(Pout4), .in(or_5_out), .sel(bitselector_7_out));  // open: out4, out6, out11, out12, out13, out14, out15, out16, out17, out18, out19, out20, out21, out22, out23, out24, out25, out26, out27, out28, out29, out30, out31
  BitSelector #(.group(5)) bitselector_7 (.in(shift_register_1_out[31:24]), .out(bitselector_7_out), .sel(1'b0));
  Register #(.width(16)) R2 (.D(demultiplexer_3_out1), .en(demultiplexer_2_out1), .Q(R2_q), .clk(ClkOut), .clr(reset));
  and and_15 (and_15_out, and_14_out, or_10_out);
  Register #(.width(16)) R3 (.D(demultiplexer_3_out2), .en(demultiplexer_2_out2), .Q(R3_q), .clk(ClkOut), .clr(reset));
  ALU ALU_1 (
    .CR(CARRY_q), .ClkIn(and_14_out), .Operand1(multiplexer_3_out), .Operand2(multiplexer_4_out),
    .Inst(bitselector_6_out), .out_6(ALU_1_out_6), .Carry(ALU_1_carry));
  or or_6 (or_6_out, and_15_out, and_16_out);
  and and_16 (and_16_out, or_8_out, and_17_out);
  Register #(.width(16)) R4 (.D(demultiplexer_3_out3), .en(demultiplexer_2_out3), .Q(R4_q), .clk(ClkOut), .clr(reset));
  Multiplexer #(.width(16)) multiplexer_5 (
    .in0(multiplexer_3_out), .in1(Stack_dout), .out(multiplexer_5_out), .sel(demultiplexer_1_out21));
  or or_7 (or_7_out, or_8_out, or_10_out);
  or or_8 (or_8_out, demultiplexer_1_out30, demultiplexer_1_out20);
  or or_9 (or_9_out, demultiplexer_1_out23, demultiplexer_1_out3, demultiplexer_1_out0, demultiplexer_1_out4);
  Register #(.width(16)) CARRY (.D(ALU_1_carry), .en(or_9_out), .Q(CARRY_q), .clk(ClkOut), .clr(reset));
  Counter #(.max('hffff), .width(16)) counter_2 (
    .count(or_7_out), .Q(counter_2_q), .up(or_8_out), .clk(or_6_out));  // open: load, D, carry, clr
  RAM #(.addrWidth(16), .dataWidth(16), .enables("line")) Stack (
    .addr(counter_2_q), .we(or_8_out), .clk(and_17_out), .din(multiplexer_3_out), .dout(Stack_dout));
  and and_17 (and_17_out, and_14_out, or_7_out);
  or or_10 (or_10_out, demultiplexer_1_out21, demultiplexer_1_out8);
  Register #(.width(1)) BR (
    .D(demultiplexer_3_out5[0]), .en(demultiplexer_2_out5), .Q(BR_q), .clk(ClkOut), .clr(reset));
  Demultiplexer #(.select(5), .width(16)) demultiplexer_3 (
    .out0(demultiplexer_3_out0), .out1(demultiplexer_3_out1), .out2(demultiplexer_3_out2),
    .out3(demultiplexer_3_out3), .out5(demultiplexer_3_out5), .out6(GPU), .out7(demultiplexer_3_out7),
    .out8(P2), .out9(P3), .out10(P4), .in(multiplexer_6_out), .sel(bitselector_9_out));  // open: out4, out11, out12, out13, out14, out15, out16, out17, out18, out19, out20, out21, out22, out23, out24, out25, out26, out27, out28, out29, out30, out31
  Multiplexer #(.select(5), .width(16)) multiplexer_6 (
    .in0(ALU_1_out_6), .in1(ALU_1_out_6), .in2(ALU_1_out_6), .in3(ALU_1_out_6), .in8(Stack_dout),
    .in14(ALU_1_out_6), .in15(ALU_1_out_6), .in16(ALU_1_out_6), .in18(bit_extender_1_out),
    .in19(multiplexer_3_out), .in23(ALU_1_out_6), .in24(ALU_1_out_6), .in25(ALU_1_out_6), .in26(ALU_1_out_6),
    .out(multiplexer_6_out), .sel(bitselector_8_out));  // open: in4, in5, in6, in7, in9, in10, in11, in12, in13, in17, in20, in21, in22, in27, in28, in29, in30, in31
  BitSelector #(.group(5)) bitselector_8 (.in(InstructionChip_data), .out(bitselector_8_out), .sel(1'b0));
  BitSelector #(.group(5)) bitselector_9 (.in(shift_register_1_out[31:24]), .out(bitselector_9_out), .sel(1'b0));
  assign P1 = demultiplexer_3_out7;  // Buffer buffer_8, 16 bits wide
  Multiplexer #(.width(16)) multiplexer_7 (
    .in0(multiplexer_5_out), .in1(multiplexer_4_out), .out(WriteValue), .sel(RequestWrite));

  // Notes on the sheet:
  //   EIPE 16 GP
  //   8 bit inst
  //   8 bit operand 1
  //   8 bit operand 2
  //   8 bit output
  //   16 bit imm
  //   contents of DebugInst (hex, n*v repeats v):
  //   12 12 4*0 13 8 4*0 1a 0 12 5 0 7 a 12 0 0 0 1e d 12 0 0 0 6 13 12 0 8 0 0 e 0 12 7 0 7f 13 12 4*0 d
  //   12 0 0 0 6
  //   Debug, can be removed
  //   contents of InstructionLUT (hex, n*v repeats v):
  //   0 1 2 3 4 5 6 7 8 9 a b c d e f 10 11 16 17 18 19 1a 1b 1c 1d 1e 1f 20 21 22 23 20 21 22 23 24 25
  //   contents of InstructionChip (hex, n*v repeats v):
  //   0 1 2 3 4 5 6 7 8 9 a b c d e f 10 1f 14 11 15 1e 12 13 14 15 16 17 18 19 1a 1b 1c 1d 1e 1f
  //   Branching Handler
  //   Of doom, some would say
endmodule

module Motherboard (
);

  wire and_1_out, and_2_out, and_3_out, and_4_out, and_5_out, and_6_out, buffer_1_out, buffer_2_out,
       buffer_3_out, buffer_4_out, clock_1_out, comparator_1_eq, comparator_1_gt, CPU_acceptclock,
       CPU_clkout, CPU_pout1, CPU_pout2, CPU_pout3, CPU_requestjump, CPU_requestwrite, CPU_rrq,
       MemMod1_clkout, memorymanager_1_clkpassthrough, memorymanager_1_wen1, memorymanager_1_wen2,
       memorymanager_1_wen3, memorymanager_1_wen4, memorymanager_1_wen5, memorymanager_1_wen6, not_1_out,
       not_2_out, or_1_out, or_2_out, or_3_out, or_4_out, Power_out, Reset_out, rgb_video_1_p1, t_ff_1_q,
       t_ff_1_qn, t_ff_2_q, t_ff_2_qn;
  wire [6:0] keyboard_1_data;
  wire [7:0] MemMod1_dout1, MemMod1_dout2, MemMod1_dout3, MemMod1_dout4, MemMod1_dout5, MemMod1_dout6,
       memorymanager_1_a1, memorymanager_1_a2, memorymanager_1_a3, memorymanager_1_a4, memorymanager_1_a5,
       memorymanager_1_a6, memorymanager_1_dout1, memorymanager_1_dout2, memorymanager_1_dout3,
       memorymanager_1_dout4, memorymanager_1_dout5, memorymanager_1_dout6;
  wire [7:7] keyboard_1_avail;
  wire [15:0] adder_1_out, bit_extender_1_out, CPU_p1, CPU_p3, CPU_writevalue, demultiplexer_1_out0,
       demultiplexer_1_out1, multiplexer_1_out, register_1_q, rgb_video_1_p4;

  Clock clock_1 (.out(clock_1_out));
  Button Power (.out(Power_out));
  Button Reset (.out(Reset_out));
  assign bit_extender_1_out = {{12{1'b0}}, 4'b0110};  // Bit_Extender bit_extender_1
  T_Flip_Flop t_ff_1 (.clk(Power_out), .T(Power_out), .Q(t_ff_1_q), .Qn(t_ff_1_qn));  // open: preset, reset
  Multiplexer #(.width(16)) multiplexer_1 (
    .in0(register_1_q), .in1(CPU_writevalue), .out(multiplexer_1_out), .sel(CPU_requestjump));
  Adder #(.width(16)) adder_1 (.a(multiplexer_1_out), .b(bit_extender_1_out), .out(adder_1_out));  // open: cin, cout
  buf buffer_1 (buffer_1_out, buffer_2_out);
  or or_1 (or_1_out, CPU_requestjump, and_1_out);
  buf buffer_2 (buffer_2_out, and_1_out);
  and and_1 (and_1_out, and_2_out, CPU_acceptclock);
  and and_2 (and_2_out, clock_1_out, t_ff_1_qn);
  Register #(.width(16)) register_1 (
    .D(adder_1_out), .en(or_1_out), .Q(register_1_q), .clk(buffer_1_out), .clr(or_2_out));
  or or_2 (or_2_out, t_ff_1_q, Reset_out);
  MemoryModule MemMod1 (
    .aIn1(memorymanager_1_a6), .dIn1(memorymanager_1_dout1), .wIn1(memorymanager_1_wen1),
    .aIn2(memorymanager_1_a5), .dIn2(memorymanager_1_dout2), .wIn2(memorymanager_1_wen2),
    .aIn3(memorymanager_1_a4), .dIn3(memorymanager_1_dout3), .wIn3(memorymanager_1_wen3),
    .aIn4(memorymanager_1_a3), .dIn4(memorymanager_1_dout4), .wIn4(memorymanager_1_wen4),
    .aIn5(memorymanager_1_a2), .dIn5(memorymanager_1_dout5), .wIn5(memorymanager_1_wen5),
    .aIn6(memorymanager_1_a1), .dIn6(memorymanager_1_dout6), .wIn6(memorymanager_1_wen6), .clk(or_3_out),
    .dOut1(MemMod1_dout1), .dOut2(MemMod1_dout2), .dOut3(MemMod1_dout3), .dOut4(MemMod1_dout4),
    .dOut5(MemMod1_dout5), .dOut6(MemMod1_dout6), .clkOut(MemMod1_clkout));
  buf buffer_3 (buffer_3_out, and_2_out);
  buf buffer_4 (buffer_4_out, buffer_3_out);
  or or_3 (or_3_out, and_3_out, and_4_out);
  MemoryManager memorymanager_1 (
    .Address(register_1_q), .WriteRq(CPU_requestwrite), .Data(CPU_writevalue), .Channels(4'b0110),
    .CDI1(MemMod1_dout1), .CDI2(MemMod1_dout2), .CDI3(MemMod1_dout3), .CDI4(MemMod1_dout4),
    .CDI5(MemMod1_dout5), .CDI6(MemMod1_dout6), .Clk(buffer_4_out), .ReadRq(CPU_rrq),
    .A1(memorymanager_1_a1), .A2(memorymanager_1_a2), .A3(memorymanager_1_a3), .A4(memorymanager_1_a4),
    .A5(memorymanager_1_a5), .A6(memorymanager_1_a6), .dOut1(memorymanager_1_dout1),
    .wEn1(memorymanager_1_wen1), .dOut2(memorymanager_1_dout2), .wEn2(memorymanager_1_wen2),
    .dOut3(memorymanager_1_dout3), .wEn3(memorymanager_1_wen3), .dOut4(memorymanager_1_dout4),
    .wEn4(memorymanager_1_wen4), .dOut5(memorymanager_1_dout5), .wEn5(memorymanager_1_wen5),
    .dOut6(memorymanager_1_dout6), .wEn6(memorymanager_1_wen6),
    .ClkPassthrough(memorymanager_1_clkpassthrough));
  not not_1 (not_1_out, CPU_acceptclock);
  and and_3 (and_3_out, not_1_out, memorymanager_1_clkpassthrough);
  and and_4 (and_4_out, CPU_acceptclock, CPU_clkout);
  or or_4 (or_4_out, comparator_1_gt, comparator_1_eq);
  Comparator #(.mode("unsigned"), .width(4)) comparator_1 (
    .a(4'b0110), .b(4'b0110), .gt(comparator_1_gt), .eq(comparator_1_eq));  // open: lt
  and and_5 (and_5_out, or_4_out, not_2_out);
  not not_2 (not_2_out, 1'b1);
  EIPE16GP CPU (
    .SingleCycleFetch(and_5_out), .clk(memorymanager_1_clkpassthrough), .inst_6(memorymanager_1_dout6),
    .inst_5(memorymanager_1_dout5), .inst_4(memorymanager_1_dout4), .inst_3(memorymanager_1_dout3),
    .inst_2(memorymanager_1_dout2), .inst_1(memorymanager_1_dout1), .useBuiltIn(1'b1), .reset(or_2_out),
    .Interrupt(MemMod1_clkout), .Peripheral2({{8{1'b0}}, keyboard_1_avail[7], keyboard_1_data}), .P1(CPU_p1),
    .Pout1(CPU_pout1), .Pout2(CPU_pout2), .P3(CPU_p3), .Pout3(CPU_pout3), .RRQ(CPU_rrq), .ClkOut(CPU_clkout),
    .RequestJump(CPU_requestjump), .RequestWrite(CPU_requestwrite), .WriteValue(CPU_writevalue),
    .AcceptClock(CPU_acceptclock));  // open: Peripheral4, GA, Peripheral1, Peripheral3, P2, P4, Pout4, GPU
  TTY #(.cols(48), .rows(12)) tty_1 (.data(CPU_p1[6:0]), .clk(CPU_clkout), .we(CPU_pout1), .clr(and_6_out));
  and and_6 (and_6_out, CPU_clkout, CPU_p1[7]);
  Keyboard keyboard_1 (
    .clk(CPU_clkout), .re(CPU_pout2), .avail(keyboard_1_avail[7]), .data(keyboard_1_data));  // open: clr
  Demultiplexer #(.width(16)) demultiplexer_1 (
    .out0(demultiplexer_1_out0), .out1(demultiplexer_1_out1), .in(CPU_p3), .sel(t_ff_2_q));
  T_Flip_Flop t_ff_2 (.clk(CPU_clkout), .T(CPU_pout3), .Q(t_ff_2_q), .Qn(t_ff_2_qn));  // open: preset, reset
  // RGB_Video #(.cursor("No Cursor"), .height(256), .scale(1), .width(256)) rgb_video_1: pin names not known; wires that end beside it: rgb_video_1_p1, rgb_video_1_p1, rgb_video_1_p4[15:8], rgb_video_1_p4[7:0], demultiplexer_1_out1
  and and_7 (rgb_video_1_p1, CPU_clkout, CPU_pout3, t_ff_2_q);
  Register #(.width(16)) register_2 (
    .D(demultiplexer_1_out0), .en(t_ff_2_qn), .Q(rgb_video_1_p4), .clk(CPU_pout3));  // open: clr
endmodule

// Memory Manager
module MemoryManager (
  input  [15:0] Address,
  input  WriteRq,
  input  [15:0] Data,
  input  [3:0] Channels,
  input  [7:0] CDI1,
  input  [7:0] CDI2,
  input  [7:0] CDI3,
  input  [7:0] CDI4,
  input  [7:0] CDI5,
  input  [7:0] CDI6,
  input  Clk,
  input  ReadRq,
  output [7:0] A1,
  output [7:0] A2,
  output [7:0] A3,
  output [7:0] A4,
  output [7:0] A5,
  output [7:0] A6,
  output [7:0] dOut1,
  output wEn1,
  output [7:0] dOut2,
  output wEn2,
  output [7:0] dOut3,
  output wEn3,
  output [7:0] dOut4,
  output wEn4,
  output [7:0] dOut5,
  output wEn5,
  output [7:0] dOut6,
  output wEn6,
  output ClkPassthrough
);

  wire comparator_1_gt, comparator_2_gt, comparator_3_gt, comparator_4_gt, comparator_5_gt, comparator_6_gt,
       comparator_7_gt;
  wire [2:0] multiplexer_2_out;
  wire [7:0] bit_extender_2_out, bitselector_1_out, subtractor_1_out;
  wire [15:0] bit_extender_1_out, divider_1_out, divider_1_rem, multiplexer_1_out;

  Multiplexer #(.width(16)) multiplexer_1 (.in0(Address), .in1(Data), .out(multiplexer_1_out), .sel(ReadRq));
  assign bit_extender_1_out = {{12{1'b0}}, Channels};  // Bit_Extender bit_extender_1
  Bit_Extender #(.in_width(16), .out_width(8), .\type ("zero")) bit_extender_2 (.in(Data), .out(bit_extender_2_out));
  Divider #(.width(16)) divider_1 (
    .a(multiplexer_1_out), .b(bit_extender_1_out), .out(divider_1_out), .rem(divider_1_rem));  // open: upper
  Decoder #(.select(3)) decoder_1 (
    .out0(wEn1), .out1(wEn2), .out2(wEn3), .out3(wEn4), .out4(wEn5), .out5(wEn6), .sel(divider_1_rem[2:0]),
    .en(WriteRq));  // open: out6, out7
  Comparator #(.mode("unsigned"), .width(3)) comparator_1 (
    .a(divider_1_out[2:0]), .b(3'b000), .gt(comparator_1_gt));  // open: eq, lt
  // Probe on bitselector_1_out
  BitSelector #(.group(8), .width(16)) bitselector_1 (.in(divider_1_out), .out(bitselector_1_out), .sel(1'b0));
  // Probe on multiplexer_2_out
  Multiplexer #(.width(3)) multiplexer_2 (
    .in0(bit_extender_1_out[2:0]), .in1(divider_1_rem[2:0]), .out(multiplexer_2_out), .sel(comparator_1_gt));
  Subtractor subtractor_1 (.a(bitselector_1_out), .b(8'h1), .out(subtractor_1_out));  // open: bin, bout
  Comparator #(.mode("unsigned"), .width(3)) comparator_2 (
    .a(3'b000), .b(multiplexer_2_out), .gt(comparator_2_gt));  // open: eq, lt
  Comparator #(.mode("unsigned"), .width(3)) comparator_3 (
    .a(3'b001), .b(multiplexer_2_out), .gt(comparator_3_gt));  // open: eq, lt
  Comparator #(.mode("unsigned"), .width(3)) comparator_4 (
    .a(3'b010), .b(multiplexer_2_out), .gt(comparator_4_gt));  // open: eq, lt
  Comparator #(.mode("unsigned"), .width(3)) comparator_5 (
    .a(3'b011), .b(multiplexer_2_out), .gt(comparator_5_gt));  // open: eq, lt
  Comparator #(.mode("unsigned"), .width(3)) comparator_6 (
    .a(3'b100), .b(multiplexer_2_out), .gt(comparator_6_gt));  // open: eq, lt
  Comparator #(.mode("unsigned"), .width(3)) comparator_7 (
    .a(3'b101), .b(multiplexer_2_out), .gt(comparator_7_gt));  // open: eq, lt
  Multiplexer #(.width(8)) multiplexer_3 (.in0(CDI5), .in1(bit_extender_2_out), .out(dOut5), .sel(wEn5));
  Multiplexer #(.width(8)) multiplexer_4 (.in0(CDI6), .in1(bit_extender_2_out), .out(dOut6), .sel(wEn6));
  Multiplexer #(.width(8)) multiplexer_5 (
    .in0(bitselector_1_out), .in1(subtractor_1_out), .out(A2), .sel(comparator_3_gt));
  Multiplexer #(.width(8)) multiplexer_6 (
    .in0(bitselector_1_out), .in1(subtractor_1_out), .out(A4), .sel(comparator_5_gt));
  Multiplexer #(.width(8)) multiplexer_7 (
    .in0(bitselector_1_out), .in1(subtractor_1_out), .out(A6), .sel(comparator_7_gt));
  Multiplexer #(.width(8)) multiplexer_8 (.in0(CDI3), .in1(bit_extender_2_out), .out(dOut3), .sel(wEn3));
  Multiplexer #(.width(8)) multiplexer_9 (.in0(CDI4), .in1(bit_extender_2_out), .out(dOut4), .sel(wEn4));
  Multiplexer #(.width(8)) multiplexer_10 (
    .in0(bitselector_1_out), .in1(subtractor_1_out), .out(A1), .sel(comparator_2_gt));
  Multiplexer #(.width(8)) multiplexer_11 (
    .in0(bitselector_1_out), .in1(subtractor_1_out), .out(A3), .sel(comparator_4_gt));
  Multiplexer #(.width(8)) multiplexer_12 (
    .in0(bitselector_1_out), .in1(subtractor_1_out), .out(A5), .sel(comparator_6_gt));
  Multiplexer #(.width(8)) multiplexer_13 (.in0(CDI1), .in1(bit_extender_2_out), .out(dOut1), .sel(wEn1));
  Multiplexer #(.width(8)) multiplexer_14 (.in0(CDI2), .in1(bit_extender_2_out), .out(dOut2), .sel(wEn2));

  assign ClkPassthrough = Clk;

  // Notes on the sheet:
  //   TODO:
  //   Add the ability to have values bigger than 16 bits support
endmodule

module ALU (
  input  [15:0] CR,
  input  ClkIn,
  input  [15:0] Operand1,
  input  [15:0] Operand2,
  input  [4:0] Inst,
  output [15:0] out_6,
  output [15:0] Carry
);

  wire adder_1_cout, buffer_1_out, buffer_2_out, comparator_1_gt, not_1_out, subtractor_1_bout;
  wire [15:0] adder_1_out, and_1_out, and_2_out, and_3_out, bit_extender_1_out, bitselector_1_out,
       bitselector_2_out, multiplier_1_cout, multiplier_1_out, nand_1_out, not_2_out, register_1_q,
       shifter_1_out, shifter_2_out, shifter_3_out, shifter_4_out, subtractor_1_out, xor_1_out;

  Register #(.width(16)) register_1 (.D(CR), .en(buffer_1_out), .Q(register_1_q), .clk(buffer_1_out), .clr(not_1_out));
  buf buffer_1 (buffer_1_out, buffer_2_out);
  buf buffer_2 (buffer_2_out, ClkIn);
  not not_1 (not_1_out, ClkIn);
  assign and_1_out = Operand1 & Operand2;  // AND_Gate and_1, 16 bits wide
  Adder #(.width(16)) adder_1 (
    .a(Operand1), .b(Operand2), .out(adder_1_out), .cin(register_1_q[0]), .cout(adder_1_cout));
  Subtractor #(.width(16)) subtractor_1 (
    .a(Operand1), .b(Operand2), .out(subtractor_1_out), .bin(register_1_q[0]), .bout(subtractor_1_bout));
  assign nand_1_out = ~(Operand1 & Operand2);  // NAND_Gate nand_1, 16 bits wide
  Multiplier #(.width(16)) multiplier_1 (
    .a(Operand1), .b(Operand2), .out(multiplier_1_out), .cin(register_1_q), .cout(multiplier_1_cout));
  assign xor_1_out = Operand1 ^ Operand2;  // XOR_Gate xor_1, 16 bits wide
  Shifter #(.width(16)) shifter_1 (.in(Operand1), .\dist (Operand2[3:0]), .out(shifter_1_out));
  Comparator #(.mode("unsigned"), .width(12)) comparator_1 (
    .a(Operand2[15:4]), .b({12{1'b0}}), .gt(comparator_1_gt));  // open: eq, lt
  Shifter #(.shift("rl"), .width(16)) shifter_2 (.in(Operand1), .\dist (Operand2[3:0]), .out(shifter_2_out));
  Shifter #(.shift("lr"), .width(16)) shifter_3 (.in(Operand1), .\dist (Operand2[3:0]), .out(shifter_3_out));
  assign bit_extender_1_out = {{15{1'b1}}, comparator_1_gt};  // Bit_Extender bit_extender_1
  Shifter #(.shift("rr"), .width(16)) shifter_4 (.in(Operand1), .\dist (Operand2[3:0]), .out(shifter_4_out));
  assign not_2_out = ~bit_extender_1_out;  // NOT_Gate not_2, 16 bits wide
  assign and_2_out = not_2_out & shifter_1_out;  // AND_Gate and_2, 16 bits wide
  assign and_3_out = not_2_out & shifter_3_out;  // AND_Gate and_3, 16 bits wide
  BitSelector #(.group(16), .width(1)) bitselector_1 (.in(adder_1_cout), .out(bitselector_1_out), .sel(1'b0));
  BitSelector #(.group(16), .width(1)) bitselector_2 (.in(subtractor_1_bout), .out(bitselector_2_out), .sel(1'b0));
  Multiplexer #(.select(5), .width(16)) multiplexer_1 (
    .in0(adder_1_out), .in1(adder_1_out), .in2(subtractor_1_out), .in3(subtractor_1_out),
    .in4(multiplier_1_out), .in5(multiplier_1_out), .in14(and_1_out), .in15(nand_1_out), .in16(xor_1_out),
    .in23(and_2_out), .in24(shifter_2_out), .in25(and_3_out), .in26(shifter_4_out), .out(out_6), .sel(Inst));  // open: in6, in7, in8, in9, in10, in11, in12, in13, in17, in18, in19, in20, in21, in22, in27, in28, in29, in30, in31
  Multiplexer #(.select(5), .width(16)) multiplexer_2 (
    .in0(bitselector_1_out), .in3(bitselector_2_out), .in5(multiplier_1_cout), .in23(bitselector_2_out),
    .out(Carry), .sel(Inst));  // open: in1, in2, in4, in6, in7, in8, in9, in10, in11, in12, in13, in14, in15, in16, in17, in18, in19, in20, in21, in22, in24, in25, in26, in27, in28, in29, in30, in31
endmodule

module RenderCore (
  input  [7:0] Inst,
  input  [7:0] PxPos,
  input  [7:0] PxColor,
  output [7:0] PxColorOut
);
endmodule

module GPU (
  input  [15:0] dIn,
  input  CLK
);

  wire [7:0] Pallete_dout;

  RAM #(.enables("line")) VRAM (.clk(CLK));  // open: addr, we, din, dout
  RAM #(.enables("line")) Pallete (.clk(CLK), .dout(Pallete_dout));  // open: addr, we, din
  RAM #(.enables("line")) Buffer1 (.clk(CLK), .din(Pallete_dout));  // open: addr, we, dout
  RAM #(.enables("line")) Buffer2 (.clk(CLK), .din(Pallete_dout));  // open: addr, we, dout
endmodule

module delayer (
  input  in_1,
  input  [2:0] in_2,
  output out_3
);

  wire buffer_1_out, buffer_2_out, buffer_3_out, buffer_4_out, buffer_5_out, buffer_6_out, buffer_7_out,
       buffer_8_out, buffer_9_out, buffer_10_out, buffer_11_out, buffer_12_out, buffer_13_out, buffer_14_out,
       buffer_15_out, buffer_16_out, buffer_17_out, buffer_18_out, buffer_19_out, buffer_20_out,
       buffer_21_out, buffer_22_out, buffer_23_out, buffer_24_out, buffer_25_out, buffer_26_out,
       buffer_27_out, buffer_28_out, buffer_29_out, buffer_30_out, buffer_31_out, buffer_32_out,
       buffer_33_out, buffer_34_out, buffer_35_out, buffer_36_out, buffer_37_out, buffer_38_out,
       buffer_39_out, buffer_40_out, buffer_41_out, buffer_42_out, buffer_43_out, buffer_44_out,
       buffer_45_out, buffer_46_out, buffer_47_out, buffer_48_out, buffer_49_out, buffer_50_out,
       buffer_51_out, buffer_52_out, buffer_53_out, buffer_54_out, buffer_55_out, buffer_56_out,
       buffer_57_out, buffer_58_out, buffer_59_out, buffer_60_out, buffer_61_out, buffer_62_out,
       buffer_63_out, buffer_64_out, buffer_65_out, buffer_66_out, buffer_67_out, buffer_68_out,
       buffer_69_out, buffer_70_out, buffer_71_out, buffer_72_out, buffer_73_out, buffer_74_out,
       buffer_75_out, buffer_76_out, buffer_77_out, buffer_78_out, buffer_79_out, buffer_80_out,
       buffer_81_out, buffer_82_out, buffer_83_out, buffer_84_out, buffer_85_out, buffer_86_out,
       buffer_87_out, buffer_88_out, buffer_89_out, buffer_90_out, buffer_91_out, buffer_92_out,
       buffer_93_out, buffer_94_out, buffer_95_out, buffer_96_out, buffer_97_out, buffer_98_out,
       buffer_99_out, buffer_100_out, buffer_101_out, buffer_102_out, buffer_103_out, buffer_104_out,
       buffer_105_out, buffer_106_out, buffer_107_out, buffer_108_out, buffer_109_out, buffer_110_out,
       buffer_111_out, buffer_112_out, buffer_113_out, buffer_114_out, buffer_115_out, buffer_116_out,
       buffer_117_out, buffer_118_out, buffer_119_out, buffer_120_out;

  buf buffer_1 (buffer_1_out, buffer_3_out);
  buf buffer_2 (buffer_2_out, buffer_5_out);
  buf buffer_3 (buffer_3_out, buffer_7_out);
  buf buffer_4 (buffer_4_out, buffer_1_out);
  buf buffer_5 (buffer_5_out, buffer_9_out);
  buf buffer_6 (buffer_6_out, buffer_2_out);
  buf buffer_7 (buffer_7_out, buffer_11_out);
  buf buffer_8 (buffer_8_out, buffer_4_out);
  buf buffer_9 (buffer_9_out, buffer_13_out);
  buf buffer_10 (buffer_10_out, buffer_6_out);
  buf buffer_11 (buffer_11_out, buffer_15_out);
  buf buffer_12 (buffer_12_out, buffer_8_out);
  buf buffer_13 (buffer_13_out, buffer_17_out);
  buf buffer_14 (buffer_14_out, buffer_10_out);
  buf buffer_15 (buffer_15_out, buffer_19_out);
  buf buffer_16 (buffer_16_out, buffer_12_out);
  buf buffer_17 (buffer_17_out, buffer_21_out);
  buf buffer_18 (buffer_18_out, buffer_14_out);
  buf buffer_19 (buffer_19_out, buffer_23_out);
  buf buffer_20 (buffer_20_out, buffer_16_out);
  buf buffer_21 (buffer_21_out, buffer_25_out);
  buf buffer_22 (buffer_22_out, buffer_18_out);
  buf buffer_23 (buffer_23_out, buffer_27_out);
  buf buffer_24 (buffer_24_out, buffer_20_out);
  buf buffer_25 (buffer_25_out, buffer_29_out);
  buf buffer_26 (buffer_26_out, buffer_22_out);
  buf buffer_27 (buffer_27_out, buffer_31_out);
  buf buffer_28 (buffer_28_out, buffer_24_out);
  buf buffer_29 (buffer_29_out, buffer_33_out);
  buf buffer_30 (buffer_30_out, buffer_26_out);
  buf buffer_31 (buffer_31_out, buffer_35_out);
  buf buffer_32 (buffer_32_out, buffer_28_out);
  buf buffer_33 (buffer_33_out, buffer_37_out);
  buf buffer_34 (buffer_34_out, buffer_30_out);
  buf buffer_35 (buffer_35_out, buffer_39_out);
  buf buffer_36 (buffer_36_out, buffer_32_out);
  buf buffer_37 (buffer_37_out, buffer_41_out);
  buf buffer_38 (buffer_38_out, buffer_34_out);
  buf buffer_39 (buffer_39_out, buffer_43_out);
  buf buffer_40 (buffer_40_out, buffer_36_out);
  buf buffer_41 (buffer_41_out, buffer_45_out);
  buf buffer_42 (buffer_42_out, buffer_38_out);
  buf buffer_43 (buffer_43_out, buffer_47_out);
  buf buffer_44 (buffer_44_out, buffer_40_out);
  buf buffer_45 (buffer_45_out, buffer_49_out);
  buf buffer_46 (buffer_46_out, buffer_42_out);
  buf buffer_47 (buffer_47_out, buffer_51_out);
  buf buffer_48 (buffer_48_out, buffer_44_out);
  buf buffer_49 (buffer_49_out, buffer_53_out);
  buf buffer_50 (buffer_50_out, buffer_46_out);
  buf buffer_51 (buffer_51_out, buffer_55_out);
  buf buffer_52 (buffer_52_out, buffer_48_out);
  buf buffer_53 (buffer_53_out, buffer_57_out);
  buf buffer_54 (buffer_54_out, buffer_50_out);
  buf buffer_55 (buffer_55_out, buffer_59_out);
  buf buffer_56 (buffer_56_out, buffer_52_out);
  buf buffer_57 (buffer_57_out, buffer_61_out);
  buf buffer_58 (buffer_58_out, buffer_54_out);
  buf buffer_59 (buffer_59_out, buffer_63_out);
  buf buffer_60 (buffer_60_out, buffer_56_out);
  buf buffer_61 (buffer_61_out, buffer_65_out);
  buf buffer_62 (buffer_62_out, buffer_58_out);
  buf buffer_63 (buffer_63_out, buffer_67_out);
  buf buffer_64 (buffer_64_out, buffer_60_out);
  buf buffer_65 (buffer_65_out, buffer_69_out);
  buf buffer_66 (buffer_66_out, buffer_62_out);
  buf buffer_67 (buffer_67_out, buffer_71_out);
  buf buffer_68 (buffer_68_out, buffer_64_out);
  buf buffer_69 (buffer_69_out, buffer_73_out);
  buf buffer_70 (buffer_70_out, buffer_66_out);
  buf buffer_71 (buffer_71_out, buffer_75_out);
  buf buffer_72 (buffer_72_out, buffer_68_out);
  buf buffer_73 (buffer_73_out, buffer_77_out);
  buf buffer_74 (buffer_74_out, buffer_70_out);
  buf buffer_75 (buffer_75_out, in_1);
  buf buffer_76 (buffer_76_out, buffer_72_out);
  buf buffer_77 (buffer_77_out, buffer_79_out);
  buf buffer_78 (buffer_78_out, buffer_74_out);
  buf buffer_79 (buffer_79_out, buffer_76_out);
  buf buffer_80 (buffer_80_out, buffer_78_out);
  buf buffer_81 (buffer_81_out, buffer_82_out);
  buf buffer_82 (buffer_82_out, buffer_84_out);
  buf buffer_83 (buffer_83_out, buffer_81_out);
  buf buffer_84 (buffer_84_out, buffer_86_out);
  buf buffer_85 (buffer_85_out, buffer_83_out);
  buf buffer_86 (buffer_86_out, buffer_88_out);
  buf buffer_87 (buffer_87_out, buffer_85_out);
  buf buffer_88 (buffer_88_out, buffer_90_out);
  buf buffer_89 (buffer_89_out, buffer_87_out);
  buf buffer_90 (buffer_90_out, buffer_92_out);
  buf buffer_91 (buffer_91_out, buffer_89_out);
  buf buffer_92 (buffer_92_out, buffer_94_out);
  buf buffer_93 (buffer_93_out, buffer_91_out);
  buf buffer_94 (buffer_94_out, buffer_96_out);
  buf buffer_95 (buffer_95_out, buffer_93_out);
  buf buffer_96 (buffer_96_out, buffer_98_out);
  buf buffer_97 (buffer_97_out, buffer_95_out);
  buf buffer_98 (buffer_98_out, buffer_100_out);
  buf buffer_99 (buffer_99_out, buffer_97_out);
  buf buffer_100 (buffer_100_out, buffer_102_out);
  buf buffer_101 (buffer_101_out, buffer_99_out);
  buf buffer_102 (buffer_102_out, buffer_104_out);
  buf buffer_103 (buffer_103_out, buffer_101_out);
  buf buffer_104 (buffer_104_out, buffer_106_out);
  buf buffer_105 (buffer_105_out, buffer_103_out);
  buf buffer_106 (buffer_106_out, buffer_108_out);
  buf buffer_107 (buffer_107_out, buffer_105_out);
  buf buffer_108 (buffer_108_out, buffer_110_out);
  buf buffer_109 (buffer_109_out, buffer_107_out);
  buf buffer_110 (buffer_110_out, buffer_112_out);
  buf buffer_111 (buffer_111_out, buffer_109_out);
  buf buffer_112 (buffer_112_out, buffer_114_out);
  buf buffer_113 (buffer_113_out, buffer_111_out);
  buf buffer_114 (buffer_114_out, buffer_116_out);
  buf buffer_115 (buffer_115_out, buffer_113_out);
  buf buffer_116 (buffer_116_out, buffer_118_out);
  buf buffer_117 (buffer_117_out, buffer_115_out);
  buf buffer_118 (buffer_118_out, buffer_80_out);
  buf buffer_119 (buffer_119_out, buffer_117_out);
  buf buffer_120 (buffer_120_out, buffer_119_out);
  Multiplexer #(.select(3)) multiplexer_1 (
    .in0(buffer_1_out), .in1(buffer_79_out), .in2(buffer_2_out), .in3(buffer_80_out), .in4(buffer_81_out),
    .in5(buffer_120_out), .out(out_3), .sel(in_2));  // open: in6, in7

  // Notes on the sheet:
  //   Do not stare directly at the tower
endmodule

module TestingGrounds (
  input  in_1,
  input  [3:0] in_2
);

  wire signaldelayer_1_p3;

  // SignalDelayer signaldelayer_1: pin names not known; wires that end beside it: in_1, in_2, signaldelayer_1_p3
endmodule

module MemoryModule (
  input  [7:0] aIn1,
  input  [7:0] dIn1,
  input  wIn1,
  input  [7:0] aIn2,
  input  [7:0] dIn2,
  input  wIn2,
  input  [7:0] aIn3,
  input  [7:0] dIn3,
  input  wIn3,
  input  [7:0] aIn4,
  input  [7:0] dIn4,
  input  wIn4,
  input  [7:0] aIn5,
  input  [7:0] dIn5,
  input  wIn5,
  input  [7:0] aIn6,
  input  [7:0] dIn6,
  input  wIn6,
  input  clk,
  output [7:0] dOut1,
  output [7:0] dOut2,
  output [7:0] dOut3,
  output [7:0] dOut4,
  output [7:0] dOut5,
  output [7:0] dOut6,
  output clkOut
);

  buf buffer_1 (clkOut, clk);
  RAM #(.enables("line")) RAM_1 (.addr(aIn1), .we(wIn1), .clk(clkOut), .din(dIn1), .dout(dOut1));
  RAM #(.enables("line")) RAM_2 (.addr(aIn2), .we(wIn2), .clk(clkOut), .din(dIn2), .dout(dOut2));
  RAM #(.enables("line")) RAM_4 (.addr(aIn3), .we(wIn3), .clk(clkOut), .din(dIn3), .dout(dOut3));
  RAM #(.enables("line")) RAM_3 (.addr(aIn4), .we(wIn4), .clk(clkOut), .din(dIn4), .dout(dOut4));
  RAM #(.enables("line")) RAM_5 (.addr(aIn5), .we(wIn5), .clk(clkOut), .din(dIn5), .dout(dOut5));
  RAM #(.enables("line")) RAM_6 (.addr(aIn6), .we(wIn6), .clk(clkOut), .din(dIn6), .dout(dOut6));
endmodule

// VHDL entity SignalDelayer, as the project stores it:
--------------------------------------------------------------------------------
-- Project :
-- Signal Delayer
-- File    :
-- SignalDelayer
-- Autor   :
-- Comple (CompleCwaft)
-- Date    :
-- 3/29/26
--
--------------------------------------------------------------------------------
-- Description :
-- Delays a signal from propogating in 250 tick intervals
--
--------------------------------------------------------------------------------

LIBRARY ieee;
USE ieee.std_logic_1164.all;
ENTITY SignalDelayer IS
  PORT (
  ------------------------------------------------------------------------------
  --Insert input ports below
    clock      : IN  std_logic;                    -- input bit example
    val        : IN  std_logic_vector(3 DOWNTO 0); -- input vector example
  ------------------------------------------------------------------------------
  --Insert output ports below
    clockOut  : OUT std_logic                      -- output bit example
  );
END SignalDelayer;

--------------------------------------------------------------------------------
--Complete your VHDL description below
--------------------------------------------------------------------------------

ARCHITECTURE TypeArchitecture OF SignalDelayer IS

BEGIN
    p_Process: PROCESS (clock) BEGIN
        clockOut = clock;
    END PROCESS p_Process;

END TypeArchitecture;
